// Logisim project 8-bitPJ_FINAL.circ as structural Verilog: 17 circuits, main circuit main
module main (
  input  in_1,
  input  [7:0] A,
  input  in_3,
  input  [7:0] B,
  input  in_5,
  input  [1:0] OpSel,
  output [7:0] Result
);

  wire clock_1_out;
  wire [3:0] multiplexer_1_out;
  wire [7:0] RegA_q, RegB_q;

  Clock clock_1 (.out(clock_1_out));
  Register RegA (.D(A), .en(in_3), .Q(RegA_q), .clk(clock_1_out));  // open: clr
  Register RegB (.D(B), .en(in_5), .Q(RegB_q), .clk(clock_1_out));  // open: clr
  _8_bit_ALU u_8_bit_alu_1 (
    .in_1(in_1), .A(RegA_q), .B(RegB_q), .Result(Result), .Opcode(multiplexer_1_out));  // open: out_5, out_6
  Multiplexer #(.select(2), .width(4)) multiplexer_1 (
    .in0(4'b0000), .in1(4'b0101), .in2(4'b1001), .out(multiplexer_1_out), .sel(OpSel));  // open: in3, en
endmodule

module Full_Adder (
  input  Cin,
  input  A,
  input  B,
  output Sum,
  output Out
);

  wire AND_2_out, AND_out, XOR_out;

  and AND (AND_out, A, B);
  xor XOR (XOR_out, A, B);
  or OR (Out, AND_out, AND_2_out);
  and AND_2 (AND_2_out, Cin, XOR_out);
  xor XOR_2 (Sum, Cin, XOR_out);
endmodule

module _8_bit_Adder_Subtractor (
  input  Add_Subtract_Control,
  input  [7:0] A,
  input  [7:0] B,
  output [7:0] Result,
  output Carry_Out,
  output Overflow
);

  wire _0_out, _1_out, _2_out, _3_out, _4_out, _5_out, _6_out, AND_2_out, AND_out, not_1_out, not_2_out,
       not_3_out, XOR_2_out, XOR_3_out, XOR_4_out, XOR_5_out, XOR_6_out, XOR_7_out, XOR_8_out, XOR_out;

  xor XOR (XOR_out, Add_Subtract_Control, B[0]);
  xor XOR_2 (XOR_2_out, Add_Subtract_Control, B[4]);
  xor XOR_3 (XOR_3_out, Add_Subtract_Control, B[5]);
  xor XOR_4 (XOR_4_out, Add_Subtract_Control, B[7]);
  not not_1 (not_1_out, A[7]);
  not not_2 (not_2_out, XOR_4_out);
  xor XOR_5 (XOR_5_out, Add_Subtract_Control, B[6]);
  xor XOR_6 (XOR_6_out, Add_Subtract_Control, B[3]);
  xor XOR_7 (XOR_7_out, Add_Subtract_Control, B[2]);
  xor XOR_8 (XOR_8_out, Add_Subtract_Control, B[1]);
  Full_Adder _4 (.Cin(_3_out), .A(A[4]), .B(XOR_2_out), .Out(_4_out), .Sum(Result[4]));
  Full_Adder _5 (.Cin(_4_out), .A(A[5]), .B(XOR_3_out), .Out(_5_out), .Sum(Result[5]));
  Full_Adder _6 (.Cin(_5_out), .A(A[6]), .B(XOR_5_out), .Out(_6_out), .Sum(Result[6]));
  Full_Adder _7 (.Cin(_6_out), .A(A[7]), .B(XOR_4_out), .Out(Carry_Out), .Sum(Result[7]));
  Full_Adder _3 (.Cin(_2_out), .A(A[3]), .B(XOR_6_out), .Out(_3_out), .Sum(Result[3]));
  Full_Adder _2 (.Cin(_1_out), .A(A[2]), .B(XOR_7_out), .Out(_2_out), .Sum(Result[2]));
  Full_Adder _1 (.Cin(_0_out), .A(A[1]), .B(XOR_8_out), .Out(_1_out), .Sum(Result[1]));
  Full_Adder _0 (.Cin(Add_Subtract_Control), .A(A[0]), .B(XOR_out), .Out(_0_out), .Sum(Result[0]));
  not not_3 (not_3_out, Result[6]);
  and AND (AND_out, not_3_out, A[7], XOR_4_out);
  and AND_2 (AND_2_out, Result[6], not_2_out, not_1_out);
  or OR (Overflow, AND_2_out, AND_out);
endmodule

module _8_bit_AND (
  input  [7:0] A,
  input  [7:0] B,
  output [7:0] Result
);

  and AND (Result[0], A[0], B[0]);
  and AND_2 (Result[1], A[1], B[1]);
  and AND_3 (Result[2], A[2], B[2]);
  and AND_4 (Result[3], A[3], B[3]);
  and AND_5 (Result[4], A[4], B[4]);
  and AND_6 (Result[5], A[5], B[5]);
  and AND_7 (Result[6], A[6], B[6]);
  and AND_8 (Result[7], A[7], B[7]);
endmodule

module _8_bit_OR (
  input  [7:0] A,
  input  [7:0] B,
  output [7:0] Result
);

  or OR (Result[3], A[3], B[3]);
  or OR_2 (Result[4], A[4], B[4]);
  or OR_3 (Result[5], A[5], B[5]);
  or OR_4 (Result[6], A[6], B[6]);
  or OR_5 (Result[7], A[7], B[7]);
  or OR_6 (Result[1], A[1], B[1]);
  or OR_7 (Result[2], A[2], B[2]);
  or OR_8 (Result[0], A[0], B[0]);
endmodule

module _8_bit_XOR (
  input  [7:0] A,
  input  [7:0] B,
  output [7:0] Result
);

  assign Result = A ^ B;  // XOR_Gate xor_1, 8 bits wide
endmodule

module _8_bit_NOT (
  input  [7:0] A,
  output [7:0] Result
);

  assign Result = ~A;  // NOT_Gate not_1, 8 bits wide
endmodule

module _8_bit_SHL (
  input  [7:0] A,
  output [7:0] Result
);


  assign Result = {A[6:0], 1'b0};
endmodule

module _8_bit_Comparator (
  input  [7:0] A,
  input  [7:0] B,
  output A_B,
  output A_B_2,
  output A_B_3
);

  Comparator comparator_1 (.a(B), .b(A), .gt(A_B), .eq(A_B_2), .lt(A_B_3));
endmodule

module _8_bit_SHR (
  input  [7:0] A,
  output [7:0] Result
);


  assign Result = {1'b0, A[7:1]};
endmodule

module _8_bit_INC (
  input  [7:0] A,
  output [7:0] Result,
  output Carry_Out,
  output Overflow
);

  _8_bit_Adder_Subtractor u_8_bit_adder_subtractor_1 (
    .Add_Subtract_Control(1'b0), .A(A), .B(8'h1), .Result(Result), .Carry_Out(Carry_Out), .Overflow(Overflow));
endmodule

module _8_bit_DEC (
  input  [7:0] A,
  output [7:0] Result,
  output Carry_Out,
  output Overflow
);

  _8_bit_Adder_Subtractor u_8_bit_adder_subtractor_1 (
    .Add_Subtract_Control(1'b1), .A(A), .B(8'h1), .Result(Result), .Carry_Out(Carry_Out), .Overflow(Overflow));
endmodule

module _8_bit_CLEAR (
  input  [7:0] A,
  output [7:0] Result
);


  assign Result = {8{1'b0}};
endmodule

module _8_bit_NAND (
  input  [7:0] A,
  input  [7:0] B,
  output [7:0] Result
);

  wire [7:0] and_1_out;

  assign and_1_out = A & B;  // AND_Gate and_1, 8 bits wide
  assign Result = ~and_1_out;  // NOT_Gate not_1, 8 bits wide
endmodule

module _8_bit_NOR (
  input  [7:0] A,
  input  [7:0] B,
  output [7:0] Result
);

  wire [7:0] or_1_out;

  assign or_1_out = A | B;  // OR_Gate or_1, 8 bits wide
  assign Result = ~or_1_out;  // NOT_Gate not_1, 8 bits wide
endmodule

module _8_bit_NEG (
  input  [7:0] A,
  output [7:0] Result,
  output Carry_Out,
  output Overflow
);

  wire [7:0] not_1_out;

  _8_bit_INC u_8_bit_inc_1 (.A(not_1_out), .Result(Result), .Carry_Out(Carry_Out), .Overflow(Overflow));
  assign not_1_out = ~A;  // NOT_Gate not_1, 8 bits wide
endmodule

module _8_bit_ALU (
  input  in_1,
  input  [7:0] A,
  input  [7:0] B,
  input  [3:0] Opcode,
  output out_5,
  output out_6,
  output [7:0] Result
);

  wire [2:0] COM_a_b;
  wire [7:0] ADD_SUB_result, AND_result, CLEAR_result, DEC_result, INC_result, NAND_result, NEG_result,
       NOR_result, NOT_result, OR_result, SHL_result, SHR_result, XOR_result;

  _8_bit_Adder_Subtractor ADD_SUB (
    .Add_Subtract_Control(in_1), .A(A), .B(B), .Result(ADD_SUB_result), .Carry_Out(out_5), .Overflow(out_6));
  _8_bit_INC INC (.A(A), .Result(INC_result));  // open: Carry_Out, Overflow
  _8_bit_DEC DEC (.A(A), .Result(DEC_result));  // open: Carry_Out, Overflow
  _8_bit_NEG NEG (.A(A), .Result(NEG_result));  // open: Carry_Out, Overflow
  _8_bit_NOT NOT (.A(A), .Result(NOT_result));
  _8_bit_AND AND (.A(A), .B(B), .Result(AND_result));
  _8_bit_OR OR (.A(A), .B(B), .Result(OR_result));
  _8_bit_XOR XOR (.A(A), .B(B), .Result(XOR_result));
  _8_bit_SHL SHL (.A(A), .Result(SHL_result));
  _8_bit_SHR SHR (.A(A), .Result(SHR_result));
  _8_bit_Comparator COM (.A(A), .B(B), .A_B(COM_a_b[0]), .A_B_2(COM_a_b[1]), .A_B_3(COM_a_b[2]));
  _8_bit_NAND NAND (.A(A), .B(B), .Result(NAND_result));
  _8_bit_NOR NOR (.A(A), .B(B), .Result(NOR_result));
  _8_bit_CLEAR CLEAR (.A(A), .Result(CLEAR_result));
  Multiplexer #(.select(4), .width(8)) multiplexer_1 (
    .in0(ADD_SUB_result), .in1(INC_result), .in2(DEC_result), .in3(NEG_result), .in4(NOT_result),
    .in5(AND_result), .in6(OR_result), .in7(XOR_result), .in8(SHL_result), .in9(SHR_result),
    .in10({{5{1'b0}}, COM_a_b}), .in11(NAND_result), .in12(NOR_result), .in13(CLEAR_result), .out(Result),
    .sel(Opcode));  // open: in14, in15, en
endmodule
